# Fritzing sketch relayArduino (saved by Fritzing 0.9.10b)

parts:
  Part1 = SparkFun_Beefcake_Relay_Control_Kit
  Part2 = Arduino Uno (Rev3)
  JACK1 = 2.1mm Barrel Jack with Terminal Block

nets:
  N1: Part1.NC, JACK1.POS
  N2: Part1.COMMON, JACK1.NEG
  GND: Part1.GND, Part2.GND
  N3: Part1.RELAY, Part2.D8
  VCC: Part1.VCC, Part2.5V

notes:
  To TC2 pedal jack -->
  <-- to computer USB
